# Fritzing sketch scheme (saved by Fritzing 0.9.3b)
breadboards: 1

parts:
  Arduino_UNO = Arduino Uno (Rev3)
  U1 = DS1307 [package=so08]

nets:
  N1: Arduino_UNO.A4/SDA, U1.SDA
  N2: Arduino_UNO.A5/SCL, U1.SCL
  GND: Arduino_UNO.GND, U1.GND
  5V: Arduino_UNO.5V, U1.VCC
